# Fritzing sketch schema (saved by Fritzing 0.9.3b)

parts:
  Part1 = Arduino Mega 2560 (Rev3)
  Raspberry_Pi1 = Raspberry Pi B+  # not connected
  HC-1 = HC-12 Module
  KEYPAD1 = Membrane Matrix Keypad

nets:
  N1: Part1.D11_PWM, HC-1.RXD
  N2: Part1.D10_PWM, HC-1.TXD
  N3: Part1.D9_PWM, KEYPAD1.1
  N4: Part1.D8_PWM, KEYPAD1.2
  5V: Part1.5V, HC-1.VCC
  GND: Part1.GND, HC-1.GND
  N5: Part1.D3_PWM, KEYPAD1.7
  N6: Part1.D4_PWM, KEYPAD1.6
  N7: Part1.D5_PWM, KEYPAD1.5
  N8: Part1.D6_PWM, KEYPAD1.4
  N9: Part1.D7_PWM, KEYPAD1.3

notes:
  <-   USB   ->
  <- Ethernet

custom parts:
  HC-12 Module: HC-12 433Mhz Module
  Membrane Matrix Keypad: Membrane Matrix 3x4 Keypad
