# Fritzing sketch schema (saved by Fritzing 0.9.3b)

parts:
  HC-1 = HC-12 Module
  Part1 = Arduino Nano (Rev3.0)
  KY-1 = Keyes Relay [package=THT]
  KY-2 = Keyes Relay [package=THT]
  DOTSTAR1 = DotStar Strip -- Black (60/m) [part_number=2239]
  Part2 = DHT22 module

nets:
  N1: HC-1.SET, HC-1.TXD, Part1.D11/MOSI
  N2: HC-1.RXD, Part1.D10
  GND: HC-1.GND, Part1.GND, KY-1.ground, KY-2.ground, DOTSTAR1.GND, Part2.GND
  VCC: HC-1.VCC, Part1.5V, KY-1.signal, KY-2.signal, DOTSTAR1.+5V, Part2.VCC
  N3: Part1.D2, DOTSTAR1.DI
  N4: Part1.D3, DOTSTAR1.CI
  N5: Part1.D4, KY-1.power
  N6: Part1.D5, KY-2.power
  N7: Part1.D8, Part2.DATA

custom parts:
  HC-12 Module: HC-12 433Mhz Module
  Keyes Relay: The Keyes 5V relay module is suitable for SCM development, home appliance control. It uses a 5V~12V TIL control signal which can control DC / AC signal.
  DotStar Strip -- Black (60/m): NeopixelDotStar Strip, Black, 60 pixels per meter.
